// Logisim project Muruci_Matheus_29.05_CPU_RISC.circ as structural Verilog: 8 circuits, main circuit main
// S0
module main (
);

  wire Clock_out, not_1_out, not_2_out, Overflow_q, Reset_out, uc_1_clear_pc, uc_1_clk_ac, uc_1_clk_ir,
       uc_1_clk_pc, uc_1_clk_ram, uc_1_dir, uc_1_load, uc_1_mod_end, uc_1_r_w_prime, ula_1_of, ula_1_zero,
       Zero_q;
  wire [2:0] uc_1_op_code;
  wire [3:0] AC_q, multiplexer_1_out, PC_q, ram_1_data, uc_1_endereco, uc_1_operando, ula_1_saida;
  wire [7:0] IR_q, rom_1_data;

  not not_1 (not_1_out, uc_1_load);
  // Probe on uc_1_endereco
  ROM #(.addrWidth(4)) rom_1 (.addr(PC_q), .data(rom_1_data));  // open: sel
  Counter #(.width(4), .max('hf), .trigger("falling")) PC (
    .load(uc_1_load), .D(uc_1_endereco), .count(not_1_out), .Q(PC_q), .clk(uc_1_clk_pc), .clr(uc_1_clear_pc));  // open: carry
  Clock Clock (.out(Clock_out));
  Register #(.trigger("high")) IR (.D(rom_1_data), .Q(IR_q), .clk(uc_1_clk_ir));  // open: en, clr
  UC uc_1 (
    .CLK_IR(uc_1_clk_ir), .CLK_PC(uc_1_clk_pc), .CLK_AC(uc_1_clk_ac), .CLK_RAM(uc_1_clk_ram),
    .Clock(Clock_out), .Reset(Reset_out), .Clear_PC(uc_1_clear_pc), .\Instrução (IR_q),
    .Endereco(uc_1_endereco), .Operando(uc_1_operando), .Op_code(uc_1_op_code), .Overflow(Overflow_q),
    .Zero(Zero_q), .Load(uc_1_load), .R_W_prime(uc_1_r_w_prime), .Mod_End(uc_1_mod_end), .Dir(uc_1_dir));
  Button Reset (.out(Reset_out));
  // Probe on IR_q
  Multiplexer #(.width(4), .enable("false")) multiplexer_1 (
    .in0(uc_1_operando), .in1(ram_1_data), .out(multiplexer_1_out), .sel(uc_1_mod_end));
  ULA ula_1 (
    .A(AC_q), .B(multiplexer_1_out), .Saida(ula_1_saida), .\Operação (uc_1_op_code), .OF(ula_1_of),
    .Zero(ula_1_zero), .D(uc_1_dir));
  Register #(.width(4)) AC (.D(ula_1_saida), .Q(AC_q), .clk(uc_1_clk_ac));  // open: en, clr
  D_Flip_Flop Zero (.clk(uc_1_clk_ac), .D(ula_1_zero), .Q(Zero_q));  // open: Qn, preset, en, reset
  D_Flip_Flop Overflow (.clk(uc_1_clk_ac), .D(ula_1_of), .Q(Overflow_q));  // open: Qn, preset, en, reset
  RAM #(.addrWidth(4), .dataWidth(4)) ram_1 (
    .addr(uc_1_operando), .data(ram_1_data), .clk(uc_1_clk_ram), .ld(uc_1_r_w_prime));  // open: sel, clr
  assign ram_1_data = not_2_out ? AC_q : 4'bz;  // Controlled_Buffer controlled_buffer_1
  not not_2 (not_2_out, uc_1_r_w_prime);

  // Notes on the sheet:
  //   0
  //   1
  //   2
  //   3
  //   4
  //   5
  //   6
  //   7
  //   8
  //   9
  //   A
  //   B
  //   C
  //   D
  //   E
  //   F
  //   000 0
  //   MOV
  //   MOV
  //   000 1
  //   ADD
  //   001 0
  //   001 1
  //   ADD
  //   SUB
  //   010 0
  //   010 1
  //   SUB
  //   OR
  //   011 0
  //   OR
  //   011 1
  //   NOT
  //   100 0
  //   NOT
  //   100 1
  //   SHF
  //   101 0
  //   SHF
  //   101 1
  //   JPZ
  //   110 0
  //   110 1
  //   JPO
  //   GO
  //   111 0
  //   111 1
  //   STR
  //   CONJUNTO DE INSTRUÇÕES
  //   AC <= X
  //   AC <=M(X)
  //   AC <= AC + X
  //   AC <= AC + M(X)
  //   AC <= AC - X
  //   AC <= AC - M(X)
  //   AC <= AC OR X
  //   AC <= AC OR M(X)
  //   AC <= NOT X
  //   AC <= NOT M(X)
  //   AC <= AC << Q
  //   AC <= AC >> Q
  //   PC <= X SE FLAG Z
  //   PC <= X SE FLAG O
  //   PC <= X
  //   M(X) <= AC
  //   Memória de Programa
  //   contents of rom_1 (hex, n*v repeats v):
  //   1 a1 8 b1 10 31 d0 f2 11 f0 12 f1 e4 0 0 f3
  //   PROCESSADOR DE 4 BITS - RISC
  //   Instrução
  //   Memória de Dados
endmodule

module dec_2x4 (
  input  A,
  input  B,
  output S0,
  output S1,
  output S2,
  output S3
);

  and and_1 (S0, ~A, ~B);  // AND_Gate
  and and_2 (S1, ~A, B);  // AND_Gate
  and and_3 (S2, A, ~B);  // AND_Gate
  and and_4 (S3, A, B);
endmodule

module dec_3x8 (
  input  [2:0] in_1,
  output S0,
  output S1,
  output S2,
  output S3,
  output S4,
  output S5,
  output S6,
  output S7
);

  wire not_1_out, not_2_out, not_3_out, not_4_out, not_5_out, not_6_out, not_7_out, not_8_out, not_9_out,
       not_10_out, not_11_out, not_12_out;

  not not_1 (not_1_out, in_1[2]);
  not not_2 (not_2_out, in_1[1]);
  not not_3 (not_3_out, in_1[0]);
  not not_4 (not_4_out, in_1[2]);
  not not_5 (not_5_out, in_1[1]);
  not not_6 (not_6_out, in_1[2]);
  not not_7 (not_7_out, in_1[0]);
  not not_8 (not_8_out, in_1[2]);
  not not_9 (not_9_out, in_1[1]);
  not not_10 (not_10_out, in_1[0]);
  not not_11 (not_11_out, in_1[1]);
  not not_12 (not_12_out, in_1[0]);
  and and_1 (S7, in_1[2], in_1[1], in_1[0]);
  and and_2 (S0, not_1_out, not_2_out, not_3_out);
  and and_3 (S1, not_4_out, not_5_out, in_1[0]);
  and and_4 (S2, not_6_out, in_1[1], not_7_out);
  and and_5 (S3, not_8_out, in_1[1], in_1[0]);
  and and_6 (S4, in_1[2], not_9_out, not_10_out);
  and and_7 (S5, in_1[2], not_11_out, in_1[0]);
  and and_8 (S6, in_1[2], in_1[1], not_12_out);
endmodule

module soma (
  input  A,
  input  B,
  input  Vem1,
  output S,
  output Vai1
);

  wire and_1_out, and_2_out, and_3_out, xor_1_out;

  xor xor_1 (xor_1_out, A, Vem1);
  and and_1 (and_1_out, A, Vem1);
  and and_2 (and_2_out, A, B);
  and and_3 (and_3_out, Vem1, B);
  xor xor_2 (S, B, xor_1_out);
  or or_1 (Vai1, and_1_out, and_2_out, and_3_out);
endmodule

module soma_4bits (
  input  [3:0] A,
  input  [3:0] B,
  input  in_3,
  output OverFlow,
  output [3:0] Soma
);

  wire soma_2_vai1, soma_3_vai1, soma_4_vai1;

  // Probe on B
  soma soma_1 (.S(Soma[3]), .Vai1(OverFlow), .A(A[3]), .B(B[3]), .Vem1(soma_2_vai1));
  // Probe on Soma
  soma soma_2 (.S(Soma[2]), .Vai1(soma_2_vai1), .A(A[2]), .B(B[2]), .Vem1(soma_3_vai1));
  soma soma_3 (.S(Soma[1]), .Vai1(soma_3_vai1), .A(A[1]), .B(B[1]), .Vem1(soma_4_vai1));
  soma soma_4 (.S(Soma[0]), .Vai1(soma_4_vai1), .A(A[0]), .B(B[0]), .Vem1(in_3));
  // Probe on A
endmodule

module OR_4bits (
  input  [3:0] A,
  input  [3:0] B,
  output [3:0] out_3
);

  or or_1 (out_3[3], A[3], B[3]);
  or or_2 (out_3[2], A[2], B[2]);
  or or_3 (out_3[1], A[1], B[1]);
  or or_4 (out_3[0], A[0], B[0]);
endmodule

module ULA (
  input  D,
  input  [3:0] A,
  input  [3:0] B,
  input  [2:0] \Operação ,
  output [3:0] Saida,
  output Zero,
  output OF
);

  wire and_1_out, and_2_out, dec_3x8_1_s0, dec_3x8_1_s1, dec_3x8_1_s2, dec_3x8_1_s3, dec_3x8_1_s4,
       dec_3x8_1_s5, dec_3x8_1_s6, dec_3x8_1_s7, not_1_out, soma_4bits_1_overflow, subtractor_1_bout;
  wire [3:0] controlled_buffer_5_out, or_4bits_1_out_3, shifter_1_out, shifter_2_out, soma_4bits_1_soma,
       subtractor_1_out;

  dec_3x8 dec_3x8_1 (
    .S0(dec_3x8_1_s0), .S1(dec_3x8_1_s1), .S2(dec_3x8_1_s2), .S3(dec_3x8_1_s3), .S4(dec_3x8_1_s4),
    .S5(dec_3x8_1_s5), .S6(dec_3x8_1_s6), .S7(dec_3x8_1_s7), .in_1(\Operação ));
  nor nor_1 (Zero, dec_3x8_1_s7, dec_3x8_1_s6, Saida[0], Saida[1], Saida[2], Saida[3]);
  assign Saida = dec_3x8_1_s0 ? B : 4'bz;  // Controlled_Buffer controlled_buffer_1
  and and_1 (and_1_out, dec_3x8_1_s1, soma_4bits_1_overflow);
  soma_4bits soma_4bits_1 (.B(B), .A(A), .in_3(1'b0), .OverFlow(soma_4bits_1_overflow), .Soma(soma_4bits_1_soma));
  assign Saida = dec_3x8_1_s1 ? soma_4bits_1_soma : 4'bz;  // Controlled_Buffer controlled_buffer_2
  or or_1 (OF, and_1_out, and_2_out);
  Subtractor #(.width(4)) subtractor_1 (.a(A), .b(B), .out(subtractor_1_out), .bout(subtractor_1_bout));  // open: bin
  assign Saida = dec_3x8_1_s2 ? subtractor_1_out : 4'bz;  // Controlled_Buffer controlled_buffer_3
  and and_2 (and_2_out, dec_3x8_1_s2, subtractor_1_bout);
  OR_4bits or_4bits_1 (.B(B), .A(A), .out_3(or_4bits_1_out_3));
  assign Saida = dec_3x8_1_s3 ? or_4bits_1_out_3 : 4'bz;  // Controlled_Buffer controlled_buffer_4
  assign Saida = dec_3x8_1_s4 ? ~B : 4'bz;  // Controlled_Inverter controlled_inverter_1
  Shifter #(.width(4), .shift("lr")) shifter_1 (.in(A), .\dist (B[1:0]), .out(shifter_1_out));
  Shifter #(.width(4)) shifter_2 (.in(A), .\dist (B[1:0]), .out(shifter_2_out));
  assign controlled_buffer_5_out = D ? shifter_1_out : 4'bz;  // Controlled_Buffer controlled_buffer_5
  not not_1 (not_1_out, D);
  assign controlled_buffer_5_out = not_1_out ? shifter_2_out : 4'bz;  // Controlled_Buffer controlled_buffer_6
  assign Saida = dec_3x8_1_s5 ? controlled_buffer_5_out : 4'bz;  // Controlled_Buffer controlled_buffer_7
endmodule

module UC (
  input  [7:0] \Instrução ,
  input  Clock,
  input  Reset,
  input  Zero,
  input  Overflow,
  output CLK_IR,
  output CLK_PC,
  output CLK_AC,
  output CLK_RAM,
  output Mod_End,
  output Clear_PC,
  output Dir,
  output [3:0] Endereco,
  output [3:0] Operando,
  output [2:0] Op_code,
  output R_W_prime,
  output Load
);

  wire and_5_out, GoTo_out, JC_out, JZ_out;
  wire [1:0] counter_1_q;

  Counter #(.width(2), .max('h3)) counter_1 (.Q(counter_1_q), .clk(Clock), .clr(Reset));  // open: load, D, count, carry
  and and_1 (CLK_IR, ~counter_1_q[1], ~counter_1_q[0]);  // AND_Gate
  nand Storage (R_W_prime, CLK_AC, \Instrução [7], \Instrução [6], \Instrução [5], \Instrução [4]);
  and and_2 (CLK_AC, counter_1_q[1], ~counter_1_q[0]);  // AND_Gate
  and and_3 (CLK_PC, ~counter_1_q[1], counter_1_q[0]);  // AND_Gate
  and GoTo (GoTo_out, CLK_PC, \Instrução [7], \Instrução [6], \Instrução [5], ~\Instrução [4]);  // AND_Gate
  and and_4 (CLK_RAM, counter_1_q[1], counter_1_q[0]);
  and JC (JC_out, CLK_PC, \Instrução [7], \Instrução [6], ~\Instrução [5], ~\Instrução [4], Zero);  // AND_Gate
  or or_1 (Load, GoTo_out, JC_out, JZ_out);
  and JZ (JZ_out, CLK_PC, \Instrução [7], \Instrução [6], ~\Instrução [5], \Instrução [4], Overflow);  // AND_Gate
  and and_5 (and_5_out, \Instrução [7], ~\Instrução [6], \Instrução [5]);  // AND_Gate
  and and_6 (Mod_End, ~and_5_out, \Instrução [4]);  // AND_Gate

  assign Clear_PC = Reset;
  assign Dir = \Instrução [4];
  assign Endereco = \Instrução [3:0];
  assign Op_code = \Instrução [7:5];
  assign Operando = \Instrução [3:0];
endmodule
